// Logisim project Booth_Multiplication_4Bits.circ as structural Verilog: 3 circuits, main circuit Booth
module Booth (
  input  [3:0] Multiplier,
  input  [3:0] Multiplicant
);

  wire AC_Load, AC_out, ADD_SUB, button_1_out, Initial_Load, Q_out, Qn, Qn_1, SC_Load, Shift_Signal;
  wire [2:0] SC;
  wire [3:0] AC, alu_1_output, B_q;

  Button button_1 (.out(button_1_out));
  Register #(.width(4)) B (.D(Multiplicant), .en(Initial_Load), .Q(B_q), .clk(button_1_out));  // open: clr
  Shift_Register #(.length(4)) u_AC (
    .shift(Shift_Signal), .in(AC[3]), .clk(button_1_out), .out(AC_out), .load(AC_Load), .d0(alu_1_output[3]),
    .q0(AC[3]), .d1(alu_1_output[2]), .q1(AC[2]), .d2(alu_1_output[1]), .q2(AC[1]), .d3(alu_1_output[0]),
    .q3(AC[0]));  // open: clr
  ALU alu_1 (.A(AC), .B(B_q), ._0_ADD__1_SUB(ADD_SUB), .Output(alu_1_output));
  Shift_Register #(.length(4)) Q (
    .shift(Shift_Signal), .in(AC_out), .clk(button_1_out), .out(Q_out), .load(Initial_Load),
    .d0(Multiplier[3]), .d1(Multiplier[2]), .d2(Multiplier[1]), .d3(Multiplier[0]), .q3(Qn));  // open: clr, q0, q1, q2
  Counter #(.width(3), .max('h4), .ongoal("stay")) u_SC (
    .load(SC_Load), .D(3'b100), .count(Shift_Signal), .Q(SC), .clk(button_1_out));  // open: carry, clr
  D_Flip_Flop u_Qn_1 (
    .clk(button_1_out), .D(Q_out), .Q(Qn_1), .Qn(ADD_SUB), .en(Shift_Signal), .reset(Initial_Load));  // open: preset
  Control_Unit control_unit_1 (
    .Qn(Qn), .Qn_1(Qn_1), .SC(SC), .AC_Load(AC_Load), .SC_Load(SC_Load), .Initial_Load(Initial_Load),
    .Shift_Signal(Shift_Signal), .Clock(button_1_out));
endmodule

module ALU (
  input  [3:0] A,
  input  [3:0] B,
  input  _0_ADD__1_SUB,
  output [3:0] Output
);

  wire [3:0] multiplexer_1_out, not_1_out;

  assign not_1_out = ~B;  // NOT_Gate not_1, 4 bits wide
  Multiplexer #(.width(4), .enable("false")) multiplexer_1 (
    .in0(B), .in1(not_1_out), .out(multiplexer_1_out), .sel(_0_ADD__1_SUB));
  Adder #(.width(4)) adder_1 (.a(A), .b(multiplexer_1_out), .out(Output), .cin(_0_ADD__1_SUB));  // open: cout
endmodule

module Control_Unit (
  input  Qn,
  input  Qn_1,
  input  [2:0] SC,
  input  Clock,
  output AC_Load,
  output SC_Load,
  output Initial_Load,
  output Shift_Signal
);

  wire decoder_1_out3, not_1_out, or_2_out, T1, xor_1_out;
  wire [1:0] multiplexer_1_out, Timing_q;

  xor xor_1 (xor_1_out, Qn, Qn_1);
  or or_1 (SC_Load, Initial_Load, Shift_Signal);
  Multiplexer #(.width(2), .enable("false")) multiplexer_1 (
    .in0(2'b00), .in1(2'b01), .out(multiplexer_1_out), .sel(or_2_out));
  or or_2 (or_2_out, SC[0], SC[1], SC[2]);
  and and_1 (AC_Load, xor_1_out, T1);
  Decoder #(.select(2), .enable("false")) decoder_1 (
    .out0(Initial_Load), .out1(T1), .out2(Shift_Signal), .out3(decoder_1_out3), .sel(Timing_q));
  Counter #(.width(2), .max('h3)) Timing (
    .load(decoder_1_out3), .D(multiplexer_1_out), .count(not_1_out), .Q(Timing_q), .clk(Clock));  // open: carry, clr
  not not_1 (not_1_out, decoder_1_out3);

  // Other names for the same wires on the sheet: T0 = Initial_Load; T2 = Shift_Signal
endmodule
