// Logisim project Signed_Muliplication_4Bits.circ as structural Verilog: 3 circuits, main circuit Signed Multiplier
module Signed_Multiplier (
  input  [3:0] Multiplier,
  input  [3:0] Multiplicant
);

  wire AC_Load, AC_out, ALU_Signal, B_Sign_q, button_1_out, E_q, Initial_Load, Q_Sign_q, Qn, SC_Load,
       Shift_Signal, xor_1_out;
  wire [2:0] SC;
  wire [3:0] AC, alu_1_output, B_q;

  Button button_1 (.out(button_1_out));
  Register #(.width(4)) B (.D(Multiplicant), .en(Initial_Load), .Q(B_q), .clk(button_1_out));  // open: clr
  D_Flip_Flop E (.clk(button_1_out), .D(E_q), .Q(E_q), .en(Shift_Signal));  // open: Qn, preset, reset
  ALU alu_1 (.AC(B_q), .B(AC), .Output(alu_1_output), .ALU_Controller(ALU_Signal));
  Shift_Register #(.length(4)) u_AC (
    .shift(Shift_Signal), .in(E_q), .clk(button_1_out), .out(AC_out), .load(AC_Load), .d0(alu_1_output[3]),
    .q0(AC[3]), .d1(alu_1_output[2]), .q1(AC[2]), .d2(alu_1_output[1]), .q2(AC[1]), .d3(alu_1_output[0]),
    .q3(AC[0]));  // open: clr
  Shift_Register #(.length(4)) Q (
    .shift(Shift_Signal), .in(AC_out), .clk(button_1_out), .load(Initial_Load), .d0(Multiplier[3]),
    .d1(Multiplier[2]), .d2(Multiplier[1]), .d3(Multiplier[0]), .q3(Qn));  // open: out, clr, q0, q1, q2
  D_Flip_Flop A_Sign (.clk(button_1_out), .D(xor_1_out), .en(Initial_Load));  // open: Q, Qn, preset, reset
  Counter #(.width(3), .max('h4)) u_SC (
    .load(SC_Load), .D(3'b100), .count(Shift_Signal), .Q(SC), .clk(button_1_out));  // open: carry, clr
  D_Flip_Flop B_Sign (.clk(button_1_out), .Q(B_Sign_q), .en(Initial_Load));  // open: D, Qn, preset, reset
  D_Flip_Flop Q_Sign (.clk(button_1_out), .D(xor_1_out), .Q(Q_Sign_q), .en(Initial_Load));  // open: Qn, preset, reset
  Control_Unit control_unit_1 (
    .Qn(Qn), .SC(SC), .Clock(button_1_out), .AC_Load(AC_Load), .SC_Load(SC_Load),
    .Initial_Load(Initial_Load), .Shift_Signal(Shift_Signal), .ALU_Signal(ALU_Signal));
  xor xor_1 (xor_1_out, B_Sign_q, Q_Sign_q);
endmodule

module ALU (
  input  [3:0] AC,
  input  [3:0] B,
  input  ALU_Controller,
  output [3:0] Output
);

  wire [3:0] adder_1_out;

  Adder #(.width(4)) adder_1 (.a(AC), .b(B), .out(adder_1_out));  // open: cin, cout
  assign Output = adder_1_out & {4{ALU_Controller}};  // AND_Gate and_1, 4 bits wide
endmodule

module Control_Unit (
  input  Qn,
  input  [2:0] SC,
  input  Clock,
  output ALU_Signal,
  output AC_Load,
  output SC_Load,
  output Initial_Load,
  output Shift_Signal
);

  wire decoder_1_out3, not_1_out, or_2_out, T1;
  wire [1:0] multiplexer_1_out, Timing_q;

  or or_1 (SC_Load, Initial_Load, Shift_Signal);
  Multiplexer #(.width(2), .enable("false")) multiplexer_1 (
    .in0(2'b00), .in1(2'b01), .out(multiplexer_1_out), .sel(or_2_out));
  or or_2 (or_2_out, SC[0], SC[1], SC[2]);
  and and_1 (ALU_Signal, Qn, T1);
  Decoder #(.select(2), .enable("false")) decoder_1 (
    .out0(Initial_Load), .out1(T1), .out2(Shift_Signal), .out3(decoder_1_out3), .sel(Timing_q));
  Counter #(.width(2), .max('h3)) Timing (
    .load(decoder_1_out3), .D(multiplexer_1_out), .count(not_1_out), .Q(Timing_q), .clk(Clock));  // open: carry, clr
  not not_1 (not_1_out, decoder_1_out3);
  or or_3 (AC_Load, ALU_Signal, Initial_Load);

  // Other names for the same wires on the sheet: T0 = Initial_Load; T2 = Shift_Signal
endmodule
